# Fritzing sketch oc_tank_arm (saved by Fritzing 0.9.3b)
breadboards: 1

parts:
  Raspberry_Pi_1 = Raspberry Pi 3 [part_number=RPI-3-V1.2]
  U2 = TA7291P [package=HSIP10-P-2.54(THT)]
  R2 = Resistor [tolerance=±5% resistance=10k package=THT]
  VCC1 = 4 x AAA Battery Mount
  M3 = DC Motor

nets:
  N1: Raspberry_Pi_1.GPIO17, U2.IN1
  GND: Raspberry_Pi_1.GND, U2.GND, VCC1.-
  N2: Raspberry_Pi_1.GPIO18, U2.IN2
  N3: U2.OUT1, M3.pin_1
  N4: U2.Vref, R2.Pin_0
  N5: U2.Vcc, U2.Vs, R2.Pin_1, VCC1.+
  N6: U2.OUT2, M3.pin_2

notes:
  18Pin
  GND
  17Pin
  VCC
  モータ用電源(アーム)
  Raspberry3 B
  モータドライバ回路(アーム)
  アーム用モータ

custom parts:
  TA7291P: The IC are Full-Bridge Driver. 4 modes available (CW / CCW / STOP / BRAKE) and PWM control. Output current:1.0 A (AVE.) 2.0 A (PEAK)
