# Fritzing sketch oc_tank_body (saved by Fritzing 0.9.3b)
breadboards: 1

parts:
  Raspberry_Pi_1 = Raspberry Pi 3 [part_number=RPI-3-V1.2]
  U1 = TA7291P [package=HSIP10-P-2.54(THT)]
  U2 = TA7291P [package=HSIP10-P-2.54(THT)]
  R1 = Resistor [tolerance=±5% resistance=10k package=THT]
  R2 = Resistor [tolerance=±5% resistance=10k package=THT]
  VCC1 = 4 x AAA Battery Mount
  M2 = DC Motor
  M3 = DC Motor

nets:
  N1: Raspberry_Pi_1.GPIO22, U2.IN1
  GND: Raspberry_Pi_1.GND, U1.GND, U2.GND, VCC1.-
  N2: Raspberry_Pi_1.GPIO25, U1.IN2
  N3: Raspberry_Pi_1.GPIO24, U1.IN1
  N4: Raspberry_Pi_1.GPIO23, U2.IN2
  N5: U1.OUT1, M2.pin_1
  N6: U1.Vref, R1.Pin_0
  VCC: U1.Vcc, U1.Vs, U2.Vcc, U2.Vs, R1.Pin_1, R2.Pin_1, VCC1.+
  N7: U1.OUT2, M2.pin_2
  N8: U2.OUT1, M3.pin_1
  N9: U2.Vref, R2.Pin_0
  N10: U2.OUT2, M3.pin_2

notes:
  24Pin
  23Pin
  22Pin
  GND
  25Pin
  VCC
  モータ用電源(車輪)
  Raspberry3 B
  モータドライバ回路(車輪)
  右車輪用モータ
  左車輪用モータ

custom parts:
  TA7291P: The IC are Full-Bridge Driver. 4 modes available (CW / CCW / STOP / BRAKE) and PWM control. Output current:1.0 A (AVE.) 2.0 A (PEAK)
